// Logisim project tb8.circ as structural Verilog: 1 circuit, main circuit main
module main (
);

  wire AeB0, AeB1, and_1_out, and_2_out, and_3_out, and_4_out, and_5_out, and_6_out, and_7_out, and_8_out,
       and_9_out, and_10_out, and_11_out, and_12_out, and_13_out, and_14_out, and_16_out, and_17_out,
       and_18_out, and_19_out, and_20_out, and_21_out, and_22_out, and_23_out, and_24_out, and_26_out,
       and_27_out, and_28_out, and_29_out, and_33_out, and_34_out, and_35_out, and_36_out, and_37_out,
       and_38_out, and_39_out, and_40_out, and_41_out, and_42_out, and_43_out, and_44_out, and_45_out,
       and_46_out, and_47_out, and_48_out, and_49_out, and_50_out, and_51_out, and_52_out, and_53_out,
       and_54_out, and_55_out, and_56_out, and_57_out, and_58_out, and_59_out, and_60_out, and_61_out,
       and_62_out, and_63_out, and_64_out, and_65_out, and_66_out, and_67_out, and_68_out, and_69_out,
       and_70_out, and_71_out, and_72_out, and_73_out, and_74_out, and_75_out, and_76_out, and_77_out,
       and_78_out, and_79_out, and_80_out, and_81_out, and_82_out, and_83_out, and_84_out, and_85_out,
       and_86_out, and_87_out, and_88_out, and_89_out, and_90_out, and_91_out, and_92_out, and_93_out,
       and_94_out, and_95_out, and_96_out, and_97_out, and_98_out, and_99_out, and_100_out, and_101_out,
       and_102_out, and_103_out, and_104_out, and_105_out, and_106_out, and_107_out, and_108_out,
       and_109_out, and_110_out, and_111_out, and_112_out, and_113_out, and_114_out, and_115_out,
       and_116_out, and_117_out, and_118_out, and_119_out, and_120_out, and_121_out, and_122_out,
       and_124_out, and_125_out, and_126_out, and_127_out, and_128_out, and_129_out, and_130_out,
       and_131_out, and_132_out, and_133_out, and_134_out, and_135_out, and_136_out, bits, CCLK, cef, clk_e,
       clock_1_out, clp, CMP, Cn, Cn4_0, Cn4_1, CnX, CnY, CnZ, comparator_1_eq, comparator_1_gt,
       comparator_1_lt, CPL, d_ff_2_qn, d_ff_3_qn, d_ff_4_q, d_ff_5_q, EX_out, EXC, FP0, FP1, FP2, FP3, G,
       G0, G1, INT0, JUMP_out, ld, ldi_t, m, n74193_1_pin4, n74193_1_pin12, n74193_1_pin13, n74193_2_pin4,
       n74193_2_pin5, n74193_2_pin12, n74193_2_pin13, nand_1_out, nand_2_out, nand_6_out, nand_8_out,
       nor_1_out, nor_2_out, nor_3_out, nor_4_out, nor_5_out, nor_6_out, nor_7_out, nor_8_out, nor_9_out,
       nor_10_out, nor_11_out, nor_12_out, nor_13_out, nor_14_out, nor_15_out, nor_16_out, nor_17_out,
       nor_18_out, nor_19_out, nor_20_out, nor_21_out, nor_22_out, nor_24_out, nor_28_out, not_1_out,
       not_2_out, not_3_out, not_4_out, not_5_out, not_6_out, not_7_out, not_8_out, not_9_out, not_10_out,
       not_11_out, not_12_out, not_13_out, not_14_out, not_15_out, not_16_out, not_17_out, not_18_out,
       not_19_out, not_20_out, not_21_out, not_22_out, or_1_out, or_2_out, or_3_out, or_4_out, or_8_out,
       or_9_out, or_10_out, or_11_out, or_13_out, or_14_out, or_17_out, P, P0, P1, R, R_al, RD, RUN_out, s0,
       s1, s2, s3, st, stc, STOP_out, STR_out, T_RD, T_RDI, T_WR, TADR0, TADR1, TADR2, TADR3, TADR4, TADR5,
       TADR6, TADR7, WR;
  wire [2:0] d_ff_6_q;
  wire [3:0] dipswitch_1_sw4, dipswitch_1_sw8;
  wire [4:0] pull_resistor_17_node;
  wire [5:0] T_ADR;
  wire [7:0] a, Acc_q, aHigh_q, aLow_q, alu, b, CHI, CHO, CLI, CLO, d_q, DATA, register_2_q, register_3_q,
       register_6_q, switch_8_p1, switch_16_p1, T_BUS;
  wire [7:4] Control_q;
  wire [7:6] register_1_q;
  wire [15:0] ADDRESS;

  and and_1 (and_1_out, TADR2, T_WR);
  and and_2 (and_2_out, TADR3, T_WR);
  nand nand_1 (nand_1_out, Cn, not_1_out);
  nand nand_2 (nand_2_out, CnX, not_2_out);
  D_Flip_Flop d_ff_1 (.D(CCLK), .clk(clk_e), .Q(EXC), .Qn(CCLK), .reset(R));  // open: preset
  Register #(.trigger("high")) register_1 (.D(DATA), .en(1'b1), .clk(CCLK), .Q({register_1_q, T_ADR}), .clr(R));
  Register #(.trigger("high")) register_2 (.D(T_BUS), .en(1'b1), .clk(and_1_out), .Q(register_2_q), .clr(R));
  Register #(.trigger("high")) register_3 (.D(T_BUS), .en(1'b1), .clk(and_2_out), .Q(register_3_q), .clr(R));
  not not_1 (not_1_out, m);
  and and_3 (and_3_out, a[0], a[0]);
  xor xor_1 (alu[0], nand_1_out, and_10_out);
  not not_2 (not_2_out, m);
  and and_4 (and_4_out, a[4], a[4]);
  xor xor_2 (alu[4], nand_2_out, and_14_out);
  Decoder #(.enable("false"), .select(2)) decoder_1 (
    .out0(ld), .out1(ldi_t), .out2(st), .out3(stc), .sel(register_1_q));
  assign T_BUS = and_5_out ? register_2_q : 8'bz;  // Controlled_Buffer controlled_buffer_1
  and and_5 (and_5_out, TADR2, T_RD);
  assign ADDRESS[7:0] = or_1_out ? register_2_q : 8'bz;  // Controlled_Buffer controlled_buffer_2
  or or_1 (or_1_out, and_33_out, and_34_out);
  assign ADDRESS[15:8] = or_1_out ? register_3_q : 8'bz;  // Controlled_Buffer controlled_buffer_3
  assign T_BUS = and_6_out ? register_3_q : 8'bz;  // Controlled_Buffer controlled_buffer_4
  and and_6 (and_6_out, TADR3, T_RD);
  and and_7 (and_7_out, b[0], s0);
  and and_8 (and_8_out, s1, not_5_out);
  nor nor_1 (nor_1_out, and_3_out, and_7_out, and_8_out);
  not not_3 (not_3_out, nor_1_out);
  and and_9 (and_9_out, not_1_out, nor_1_out);
  and and_10 (and_10_out, not_3_out, nor_5_out);
  nor nor_2 (nor_2_out, and_9_out, and_17_out);
  and and_11 (and_11_out, b[4], s0);
  and and_12 (and_12_out, s1, not_6_out);
  nor nor_3 (nor_3_out, and_4_out, and_11_out, and_12_out);
  not not_4 (not_4_out, nor_3_out);
  and and_13 (and_13_out, not_2_out, nor_3_out);
  and and_14 (and_14_out, not_4_out, nor_6_out);
  nor nor_4 (nor_4_out, and_13_out, and_19_out);
  assign T_BUS = T_RDI ? {2'b00, T_ADR} : 8'bz;  // Controlled_Buffer controlled_buffer_5
  and and_15 (T_RDI, ldi_t, EXC);
  not not_5 (not_5_out, b[0]);
  and and_16 (and_16_out, not_5_out, s2, a[0]);
  nor nor_5 (nor_5_out, and_16_out, and_21_out);
  and and_17 (and_17_out, not_1_out, nor_5_out, Cn);
  xor xor_3 (alu[1], nor_2_out, and_24_out);
  not not_6 (not_6_out, b[4]);
  and and_18 (and_18_out, not_6_out, s2, a[4]);
  nor nor_6 (nor_6_out, and_18_out, and_26_out);
  and and_19 (and_19_out, not_2_out, nor_6_out, CnX);
  xor xor_4 (alu[5], nor_4_out, and_29_out);
  and and_20 (and_20_out, CMP, stc);
  nor nor_7 (nor_7_out, T_ADR[3], T_ADR[4], T_ADR[5]);
  Decoder #(.select(3)) decoder_2 (
    .out0(TADR0), .out1(TADR1), .sel(T_ADR[2:0]), .en(nor_7_out));  // open: out2, out3, out4, out5, out6, out7
  and and_21 (and_21_out, a[0], b[0], s3);
  and and_22 (and_22_out, a[1], a[1]);
  not not_7 (not_7_out, nor_8_out);
  and and_23 (and_23_out, not_1_out, nor_8_out);
  and and_24 (and_24_out, not_7_out, nor_12_out);
  and and_25 (AeB0, alu[0], alu[1], alu[2], alu[3]);
  and and_26 (and_26_out, a[4], b[4], s3);
  and and_27 (and_27_out, a[5], a[5]);
  not not_8 (not_8_out, nor_10_out);
  and and_28 (and_28_out, not_2_out, nor_10_out);
  and and_29 (and_29_out, not_8_out, nor_13_out);
  and and_30 (AeB1, alu[4], alu[5], alu[6], alu[7]);
  or or_2 (or_2_out, and_20_out, st);
  and and_31 (T_WR, or_2_out, EXC);
  and and_32 (T_RD, EXC, ld);
  assign DATA = and_33_out ? T_BUS : 8'bz;  // Controlled_Buffer controlled_buffer_6
  and and_33 (and_33_out, TADR4, T_WR);
  assign T_BUS = and_34_out ? DATA : 8'bz;  // Controlled_Buffer controlled_buffer_7
  and and_34 (and_34_out, TADR4, T_RD);
  and and_35 (and_35_out, b[1], s0);
  nor nor_8 (nor_8_out, and_22_out, and_35_out, and_41_out);
  and and_36 (and_36_out, not_1_out, nor_1_out, nor_12_out);
  nor nor_9 (nor_9_out, and_23_out, and_36_out, and_43_out);
  xor xor_5 (alu[2], nor_9_out, and_44_out);
  and and_37 (and_37_out, b[5], s0);
  nor nor_10 (nor_10_out, and_27_out, and_37_out, and_45_out);
  and and_38 (and_38_out, not_2_out, nor_3_out, nor_13_out);
  nor nor_11 (nor_11_out, and_28_out, and_38_out, and_47_out);
  xor xor_6 (alu[6], nor_11_out, and_48_out);
  Register #(.trigger("high")) register_4 (.D(T_BUS), .en(1'b1), .clk(and_39_out), .Q(CLI), .clr(R));
  and and_39 (and_39_out, TADR0, T_WR);
  Register #(.trigger("high")) register_5 (.D(T_BUS), .en(1'b1), .clk(and_40_out), .Q(CHI), .clr(R));
  and and_40 (and_40_out, T_WR, TADR1);
  not not_9 (not_9_out, b[1]);
  and and_41 (and_41_out, s1, not_9_out);
  and and_42 (and_42_out, not_9_out, s2, a[1]);
  not not_10 (not_10_out, nor_14_out);
  and and_43 (and_43_out, not_1_out, Cn, nor_5_out, nor_12_out);
  and and_44 (and_44_out, not_10_out, nor_18_out);
  not not_11 (not_11_out, b[5]);
  and and_45 (and_45_out, s1, not_11_out);
  and and_46 (and_46_out, not_11_out, s2, a[5]);
  not not_12 (not_12_out, nor_16_out);
  and and_47 (and_47_out, not_2_out, CnX, nor_6_out, nor_13_out);
  and and_48 (and_48_out, not_12_out, nor_19_out);
  D_Flip_Flop d_ff_2 (.Qn(d_ff_2_qn), .preset(and_39_out), .reset(and_55_out));  // open: clk, D, Q
  D_Flip_Flop d_ff_3 (.Qn(d_ff_3_qn), .preset(and_40_out), .reset(and_55_out));  // open: clk, D, Q
  and and_49 (and_49_out, T_WR, TADR5);
  and and_50 (and_50_out, T_WR, TADR6);
  and and_51 (and_51_out, a[1], s3, b[1]);
  nor nor_12 (nor_12_out, and_42_out, and_51_out);
  and and_52 (and_52_out, not_1_out, nor_14_out);
  and and_53 (and_53_out, a[5], s3, b[5]);
  nor nor_13 (nor_13_out, and_46_out, and_53_out);
  and and_54 (and_54_out, not_2_out, nor_16_out);
  Register #(.trigger("high")) register_6 (.D(T_BUS), .en(1'b1), .clk(or_3_out), .Q(register_6_q), .clr(R));
  or or_3 (or_3_out, T_RD, T_RDI);
  not not_13 (not_13_out, or_4_out);
  or or_4 (or_4_out, d_ff_2_qn, d_ff_3_qn);
  and and_55 (and_55_out, not_13_out, CCLK);
  Register #(.trigger("high")) u_A (.D(T_BUS), .en(1'b1), .clk(and_49_out), .Q(a), .clr(R));
  Register #(.trigger("high")) u_B (.D(T_BUS), .en(1'b1), .clk(and_50_out), .Q(b), .clr(R));
  and and_56 (and_56_out, a[2], a[2]);
  and and_57 (and_57_out, b[2], s0);
  nor nor_14 (nor_14_out, and_56_out, and_57_out, and_66_out);
  and and_58 (and_58_out, not_1_out, nor_8_out, nor_18_out);
  and and_59 (and_59_out, not_1_out, nor_1_out, nor_12_out, nor_18_out);
  nor nor_15 (nor_15_out, and_52_out, and_58_out, and_59_out, and_67_out);
  xor xor_7 (alu[3], nor_15_out, and_74_out);
  and and_60 (and_60_out, a[6], a[6]);
  and and_61 (and_61_out, b[6], s0);
  nor nor_16 (nor_16_out, and_60_out, and_61_out, and_68_out);
  and and_62 (and_62_out, not_2_out, nor_10_out, nor_19_out);
  and and_63 (and_63_out, not_2_out, nor_3_out, nor_13_out, nor_19_out);
  nor nor_17 (nor_17_out, and_54_out, and_62_out, and_63_out, and_69_out);
  xor xor_8 (alu[7], nor_17_out, and_77_out);
  nand nand_3 (CPL, EXC, not_13_out);
  assign T_BUS = and_64_out ? a : 8'bz;  // Controlled_Buffer controlled_buffer_8
  and and_64 (and_64_out, TADR5, T_RD);
  assign T_BUS = and_65_out ? b : 8'bz;  // Controlled_Buffer controlled_buffer_9
  and and_65 (and_65_out, TADR6, T_RD);
  not not_14 (not_14_out, b[2]);
  and and_66 (and_66_out, s1, not_14_out);
  and and_67 (and_67_out, not_1_out, Cn, nor_5_out, nor_12_out, nor_18_out);
  not not_15 (not_15_out, b[6]);
  and and_68 (and_68_out, s1, not_15_out);
  and and_69 (and_69_out, not_2_out, CnX, nor_6_out, nor_13_out, nor_19_out);
  assign T_BUS = T_WR ? register_6_q : 8'bz;  // Controlled_Buffer controlled_buffer_10
  and and_70 (and_70_out, T_RD, TADR0);
  assign T_BUS = and_70_out ? CLO : 8'bz;  // Controlled_Buffer controlled_buffer_11
  assign ADDRESS[7:0] = CCLK ? CLO : 8'bz;  // Controlled_Buffer controlled_buffer_12
  and and_71 (and_71_out, T_RD, TADR1);
  assign T_BUS = and_71_out ? CHO : 8'bz;  // Controlled_Buffer controlled_buffer_13
  assign ADDRESS[15:8] = CCLK ? CHO : 8'bz;  // Controlled_Buffer controlled_buffer_14
  and and_72 (and_72_out, not_14_out, s2, a[2]);
  and and_73 (and_73_out, a[2], s3, b[2]);
  nor nor_18 (nor_18_out, and_72_out, and_73_out);
  not not_16 (not_16_out, nor_20_out);
  and and_74 (and_74_out, not_16_out, nor_22_out);
  and and_75 (and_75_out, not_15_out, s2, a[6]);
  and and_76 (and_76_out, a[6], s3, b[6]);
  nor nor_19 (nor_19_out, and_75_out, and_76_out);
  not not_17 (not_17_out, nor_21_out);
  and and_77 (and_77_out, not_17_out, nor_24_out);
  nand nand_4 (R, R_al, R_al);
  Register #(.trigger("high")) Control (
    .D(T_BUS), .en(1'b1), .clk(and_78_out), .Q({Control_q, s3, s2, s1, s0}), .clr(R));
  and and_78 (and_78_out, T_WR, TADR7);
  Register #(.trigger("high")) Acc (.D(alu), .en(1'b1), .clk(CCLK), .Q(Acc_q), .clr(R));
  and and_79 (and_79_out, a[3], a[3]);
  nand nand_5 (P0, nor_5_out, nor_12_out, nor_18_out, nor_22_out);
  nand nand_6 (nand_6_out, Cn, nor_5_out, nor_12_out, nor_18_out, nor_22_out);
  or or_5 (Cn4_0, ~nand_6_out, ~G0);  // OR_Gate
  and and_80 (and_80_out, a[7], a[7]);
  nand nand_7 (P1, nor_6_out, nor_13_out, nor_19_out, nor_24_out);
  nand nand_8 (nand_8_out, CnX, nor_6_out, nor_13_out, nor_19_out, nor_24_out);
  or or_6 (Cn4_1, ~nand_8_out, ~G1);  // OR_Gate
  and and_81 (and_81_out, T_WR, and_82_out);
  and and_82 (and_82_out, T_ADR[3], ~T_ADR[4], ~T_ADR[5]);  // AND_Gate
  and and_83 (and_83_out, T_WR, and_84_out);
  and and_84 (and_84_out, ~T_ADR[3], T_ADR[4], ~T_ADR[5]);  // AND_Gate
  assign T_BUS = and_85_out ? Acc_q : 8'bz;  // Controlled_Buffer controlled_buffer_15
  and and_85 (and_85_out, TADR7, T_RD);
  and and_86 (and_86_out, s1, not_18_out);
  and and_87 (and_87_out, b[3], s0);
  nor nor_20 (nor_20_out, and_79_out, and_87_out, and_86_out);
  and and_88 (and_88_out, nor_1_out, nor_12_out, nor_18_out, nor_22_out);
  and and_89 (and_89_out, s1, not_19_out);
  and and_90 (and_90_out, b[7], s0);
  nor nor_21 (nor_21_out, and_80_out, and_90_out, and_89_out);
  and and_91 (and_91_out, nor_3_out, nor_13_out, nor_19_out, nor_24_out);
  RAM #(.addrWidth(3), .databus("bidir"), .trigger("high")) ram_1 (
    .addr(T_ADR[2:0]), .we(and_81_out), .oe(and_92_out), .data(T_BUS));
  and and_92 (and_92_out, and_82_out, T_RD);
  RAM #(.addrWidth(3), .databus("bidir"), .trigger("high")) ram_2 (
    .addr(T_ADR[2:0]), .we(and_83_out), .oe(and_93_out), .data(T_BUS));
  and and_93 (and_93_out, and_84_out, T_RD);
  Comparator #(.mode("unsigned")) comparator_1 (
    .a(a), .b(b), .gt(comparator_1_gt), .eq(comparator_1_eq), .lt(comparator_1_lt));
  D_Flip_Flop d_ff_4 (.D(CnY), .clk(and_85_out), .Q(d_ff_4_q));  // open: Qn, preset, reset
  not not_18 (not_18_out, b[3]);
  and and_94 (and_94_out, not_18_out, s2, a[3]);
  and and_95 (and_95_out, a[3], s3, b[3]);
  nor nor_22 (nor_22_out, and_94_out, and_95_out);
  and and_96 (and_96_out, nor_8_out, nor_18_out, nor_22_out);
  and and_97 (and_97_out, nor_14_out, nor_22_out);
  nor nor_23 (G0, and_88_out, and_96_out, and_97_out, and_103_out);
  not not_19 (not_19_out, b[7]);
  and and_98 (and_98_out, not_19_out, s2, a[7]);
  and and_99 (and_99_out, a[7], s3, b[7]);
  nor nor_24 (nor_24_out, and_98_out, and_99_out);
  and and_100 (and_100_out, nor_10_out, nor_19_out, nor_24_out);
  and and_101 (and_101_out, nor_16_out, nor_24_out);
  nor nor_25 (G1, and_91_out, and_100_out, and_101_out, and_104_out);
  Multiplexer #(.select(2)) multiplexer_1 (
    .in0(comparator_1_eq), .in1(comparator_1_gt), .in2(comparator_1_lt), .in3(bits), .out(CMP),
    .sel(Control_q[7:6]));
  and and_102 (and_102_out, d_ff_4_q, clp);
  and and_103 (and_103_out, nor_20_out, nor_20_out);
  and and_104 (and_104_out, nor_21_out, nor_21_out);
  or or_7 (Cn, and_102_out, cef);
  not not_20 (not_20_out, Cn);
  Decoder #(.enable("false"), .select(2)) decoder_3 (
    .out0(cef), .out2(clp), .out3(m), .sel(Control_q[5:4]));  // open: out1
  // LedBar #(.inputtype("row")) ledbar_1: pin names not known; wires that end beside it: a
  // LedBar #(.inputtype("row")) ledbar_2: pin names not known; wires that end beside it: b
  // LedBar #(.inputtype("row")) ledbar_3: pin names not known; wires that end beside it: alu
  and and_105 (and_105_out, G0, P0);
  Register #(.trigger("high")) aHigh (.D(T_BUS), .en(1'b1), .clk(and_106_out), .Q(aHigh_q), .clr(R));
  and and_106 (and_106_out, FP0, T_WR);
  Register #(.trigger("high")) aLow (.D(T_BUS), .en(1'b1), .clk(and_107_out), .Q(aLow_q), .clr(R));
  and and_107 (and_107_out, FP1, T_WR);
  Register #(.trigger("high")) d (.D(T_BUS), .en(1'b1), .clk(and_108_out), .Q(d_q), .clr(R));
  and and_108 (and_108_out, FP2, T_WR);
  and and_109 (and_109_out, not_20_out, G0);
  nor nor_26 (CnX, and_105_out, and_109_out);
  Hex_Digit_Display #(.decimalPoint("false")) hex_digit_display_1 (.value(a[7:4]));
  Hex_Digit_Display #(.decimalPoint("false")) hex_digit_display_2 (.value(b[7:4]));
  Hex_Digit_Display #(.decimalPoint("false")) hex_digit_display_3 (.value(alu[7:4]));
  and and_110 (and_110_out, G1, P1);
  and and_111 (and_111_out, G0, G1, P0);
  nor nor_27 (CnY, and_110_out, and_111_out, and_112_out);
  LED led_1 (.in(aHigh_q[7]));
  LED led_2 (.in(aHigh_q[6]));
  // Switch switch_1: pin names not known; wires that end beside it: 1'b1, switch_8_p1[7], 1'b1
  // Switch switch_2: pin names not known; wires that end beside it: switch_8_p1[6], 1'b1
  Pull_Resistor pull_resistor_1 (.node(switch_8_p1[7]));
  Pull_Resistor pull_resistor_2 (.node(switch_8_p1[6]));
  LED led_3 (.in(T_BUS[7]));
  LED led_4 (.in(T_BUS[6]));
  LED u_EXC (.in(EXC));
  nor nor_28 (nor_28_out, T_ADR[3], T_ADR[4], T_ADR[5]);
  Decoder #(.select(3)) decoder_4 (
    .out2(TADR2), .out3(TADR3), .out4(TADR4), .out5(TADR5), .out6(TADR6), .out7(TADR7), .sel(T_ADR[2:0]),
    .en(nor_28_out));  // open: out0, out1
  Hex_Digit_Display #(.decimalPoint("false")) hex_digit_display_4 (.value(a[3:0]));
  Hex_Digit_Display #(.decimalPoint("false")) hex_digit_display_5 (.value(b[3:0]));
  Hex_Digit_Display #(.decimalPoint("false")) hex_digit_display_6 (.value(alu[3:0]));
  and and_112 (and_112_out, not_20_out, G0, G1);
  and and_113 (and_113_out, 1'b0, 1'b0);
  LED led_5 (.in(aHigh_q[5]));
  LED led_6 (.in(aHigh_q[4]));
  // Switch switch_3: pin names not known; wires that end beside it: switch_8_p1[5], 1'b1
  // Switch switch_4: pin names not known; wires that end beside it: switch_8_p1[4]
  Pull_Resistor pull_resistor_3 (.node(switch_8_p1[5]));
  Pull_Resistor pull_resistor_4 (.node(switch_8_p1[4]));
  LED led_7 (.in(T_BUS[5]));
  LED led_8 (.in(T_BUS[4]));
  LED led_9 (.in(T_ADR[5]));
  LED led_10 (.in(T_ADR[4]));
  LED LDI (.in(CCLK));
  nor nor_29 (RD, CCLK, and_114_out);
  and and_114 (and_114_out, TADR4, T_RD);
  nor nor_30 (WR, and_115_out, and_115_out);
  and and_115 (and_115_out, TADR4, T_WR);
  and and_116 (and_116_out, G1, 1'b0, P1);
  and and_117 (and_117_out, G0, G1, 1'b0, P0);
  nor nor_31 (CnZ, and_113_out, and_116_out, and_117_out, and_119_out);
  LED led_11 (.in(aHigh_q[3]));
  LED led_12 (.in(aHigh_q[2]));
  LED led_13 (.in(aHigh_q[1]));
  // Switch switch_5: pin names not known; wires that end beside it: 1'b1, switch_8_p1[3], 1'b1
  // Switch switch_6: pin names not known; wires that end beside it: switch_8_p1[2], 1'b1
  // Switch switch_7: pin names not known; wires that end beside it: switch_8_p1[1], 1'b1
  Pull_Resistor pull_resistor_5 (.node(switch_8_p1[3]));
  Pull_Resistor pull_resistor_6 (.node(switch_8_p1[2]));
  Pull_Resistor pull_resistor_7 (.node(switch_8_p1[1]));
  LED led_14 (.in(T_BUS[3]));
  LED led_15 (.in(T_BUS[2]));
  LED led_16 (.in(T_BUS[1]));
  LED led_17 (.in(T_ADR[3]));
  LED led_18 (.in(T_ADR[2]));
  LED led_19 (.in(T_ADR[1]));
  _74193 #(.ShowInternalStructure("true")) u_74193_1 (
    .pin1(CLI[1]), .pin2(CLO[1]), .pin3(CLO[0]), .pin4(n74193_1_pin4), .pin5(CCLK), .pin6(CLO[2]),
    .pin7(CLO[3]), .pin15(CLI[0]), .pin14(R), .pin13(n74193_1_pin13), .pin12(n74193_1_pin12), .pin11(CPL),
    .pin10(CLI[2]), .pin9(CLI[3]));
  _74193 #(.ShowInternalStructure("true")) u_74193_2 (
    .pin1(CHI[1]), .pin2(CHO[1]), .pin3(CHO[0]), .pin4(n74193_2_pin4), .pin5(n74193_2_pin5), .pin6(CHO[2]),
    .pin7(CHO[3]), .pin15(CHI[0]), .pin14(R), .pin13(n74193_2_pin13), .pin12(n74193_2_pin12), .pin11(CPL),
    .pin10(CHI[2]), .pin9(CHI[3]));
  and and_118 (and_118_out, a[7], b[7]);
  and and_119 (and_119_out, not_20_out, G0, G1, 1'b0);
  LED led_20 (.in(aHigh_q[0]));
  LED led_21 (.in(aLow_q[7]));
  LED led_22 (.in(d_q[7]));
  // Switch switch_8: pin names not known; wires that end beside it: switch_8_p1[0]
  // Switch switch_9: pin names not known; wires that end beside it: 1'b1, switch_16_p1[7], 1'b1
  Pull_Resistor pull_resistor_8 (.node(switch_8_p1[0]));
  Pull_Resistor pull_resistor_9 (.node(switch_16_p1[7]));
  LED led_23 (.in(T_BUS[0]));
  LED led_24 (.in(T_ADR[0]));
  or or_8 (or_8_out, and_118_out, and_120_out);
  or or_9 (or_9_out, and_121_out, and_124_out);
  and and_120 (and_120_out, a[6], b[6]);
  and and_121 (and_121_out, a[5], b[5]);
  and and_122 (and_122_out, 1'b0, 1'b0);
  LED led_25 (.in(aLow_q[6]));
  LED led_26 (.in(aLow_q[5]));
  LED led_27 (.in(aLow_q[4]));
  LED led_28 (.in(d_q[6]));
  LED led_29 (.in(d_q[5]));
  LED led_30 (.in(d_q[4]));
  // Switch switch_10: pin names not known; wires that end beside it: switch_16_p1[6], 1'b1
  // Switch switch_11: pin names not known; wires that end beside it: switch_16_p1[5], 1'b1
  Pull_Resistor pull_resistor_10 (.node(switch_16_p1[6]));
  Pull_Resistor pull_resistor_11 (.node(switch_16_p1[5]));
  Pull_Resistor pull_resistor_12 (.node(switch_16_p1[4]));
  Button EX (.out(EX_out));
  Button RUN (.out(RUN_out));
  D_Flip_Flop d_ff_5 (.Q(d_ff_5_q), .preset(RUN_out), .reset(STOP_out));  // open: D, clk, Qn
  and and_123 (clk_e, d_ff_5_q, clock_1_out);
  Clock clock_1 (.out(clock_1_out));
  Hex_Digit_Display #(.decimalPoint("false")) hex_digit_display_7 (.value(DATA[7:4]));
  Hex_Digit_Display #(.decimalPoint("false")) hex_digit_display_8 (.value(dipswitch_1_sw4));
  DipSwitch dipswitch_1 (
    .sw1(dipswitch_1_sw4[3]), .sw2(dipswitch_1_sw4[2]), .sw3(dipswitch_1_sw4[1]), .sw4(dipswitch_1_sw4[0]),
    .sw5(dipswitch_1_sw8[3]), .sw6(dipswitch_1_sw8[2]), .sw7(dipswitch_1_sw8[1]), .sw8(dipswitch_1_sw8[0]));
  RAM #(.addrWidth(16), .databus("bidir"), .trigger("high")) ram_3 (
    .addr(ADDRESS), .we(not_21_out), .oe(not_22_out));  // open: clk, data
  not not_21 (not_21_out, WR);
  not not_22 (not_22_out, RD);
  or or_10 (or_10_out, or_8_out, or_9_out);
  or or_11 (or_11_out, or_14_out, or_13_out);
  and and_124 (and_124_out, a[4], b[4]);
  and and_125 (and_125_out, a[3], b[3]);
  and and_126 (and_126_out, 1'b0, 1'b0, 1'b0);
  and and_127 (and_127_out, G1, 1'b0, 1'b0, P1);
  nor nor_32 (G, and_122_out, and_126_out, and_127_out, and_130_out);
  LED led_31 (.in(aLow_q[3]));
  LED led_32 (.in(aLow_q[2]));
  LED led_33 (.in(d_q[3]));
  LED led_34 (.in(d_q[2]));
  // Switch switch_12: pin names not known; wires that end beside it: switch_16_p1[4]
  // Switch switch_13: pin names not known; wires that end beside it: 1'b1, switch_16_p1[3], 1'b1
  Pull_Resistor pull_resistor_13 (.node(switch_16_p1[3]));
  Pull_Resistor pull_resistor_14 (.node(switch_16_p1[2]));
  Button STR (.out(STR_out));
  Button JUMP (.out(JUMP_out));
  Button STOP (.out(STOP_out));
  Button #(.press("passive")) RES (.out(R_al));
  Hex_Digit_Display #(.decimalPoint("false")) hex_digit_display_9 (.value(DATA[3:0]));
  Hex_Digit_Display #(.decimalPoint("false")) hex_digit_display_10 (.value(dipswitch_1_sw8));
  _74193 #(.ShowInternalStructure("true")) u_74193_3 (
    .pin1(CLI[5]), .pin2(CLO[5]), .pin3(CLO[4]), .pin4(n74193_1_pin13), .pin5(n74193_1_pin12), .pin6(CLO[6]),
    .pin7(CLO[7]), .pin15(CLI[4]), .pin14(R), .pin13(n74193_2_pin4), .pin12(n74193_2_pin5), .pin11(CPL),
    .pin10(CLI[6]), .pin9(CLI[7]));
  _74193 #(.ShowInternalStructure("true")) u_74193_4 (
    .pin1(CHI[5]), .pin2(CHO[5]), .pin3(CHO[4]), .pin4(n74193_2_pin13), .pin5(n74193_2_pin12), .pin6(CHO[6]),
    .pin7(CHO[7]), .pin15(CHI[4]), .pin14(R), .pin11(CPL), .pin10(CHI[6]), .pin9(CHI[7]));  // open: pin13, pin12
  or or_12 (bits, or_10_out, or_11_out);
  or or_13 (or_13_out, and_125_out, and_128_out);
  and and_128 (and_128_out, a[2], b[2]);
  and and_129 (and_129_out, a[1], b[1]);
  and and_130 (and_130_out, G0, G1, 1'b0, 1'b0);
  LED led_35 (.in(aLow_q[1]));
  LED led_36 (.in(aLow_q[0]));
  LED led_37 (.in(d_q[1]));
  LED led_38 (.in(d_q[0]));
  // Switch switch_14: pin names not known; wires that end beside it: switch_16_p1[2], 1'b1
  // Switch switch_15: pin names not known; wires that end beside it: switch_16_p1[1], 1'b1
  // Switch switch_16: pin names not known; wires that end beside it: switch_16_p1[0]
  Pull_Resistor pull_resistor_15 (.node(switch_16_p1[1]));
  Pull_Resistor pull_resistor_16 (.node(switch_16_p1[0]));
  D_Flip_Flop d_ff_6 (.D(1'b1), .clk(EX_out), .Q(d_ff_6_q[0]), .reset(or_17_out));  // open: Qn, preset
  D_Flip_Flop d_ff_7 (.D(1'b1), .clk(STR_out), .Q(d_ff_6_q[1]), .reset(or_17_out));  // open: Qn, preset
  D_Flip_Flop d_ff_8 (.D(1'b1), .clk(JUMP_out), .Q(d_ff_6_q[2]), .reset(or_17_out));  // open: Qn, preset
  Hex_Digit_Display #(.decimalPoint("false")) hex_digit_display_11 (.value(ADDRESS[15:12]));
  Hex_Digit_Display #(.decimalPoint("false")) hex_digit_display_12 (.value(ADDRESS[11:8]));
  or or_14 (or_14_out, and_129_out, and_131_out);
  and and_131 (and_131_out, a[0], b[0]);
  or or_15 (P, P0, P1, 1'b0, 1'b0);
  Hex_Digit_Display #(.decimalPoint("false")) hex_digit_display_13 (.value(ADDRESS[7:4]));
  Hex_Digit_Display #(.decimalPoint("false")) hex_digit_display_14 (.value(ADDRESS[3:0]));
  Hex_Digit_Display #(.decimalPoint("false")) hex_digit_display_15 (.value(T_BUS[7:4]));
  Hex_Digit_Display #(.decimalPoint("false")) hex_digit_display_16 (.value(T_BUS[3:0]));
  and and_132 (and_132_out, T_ADR[3], T_ADR[4], T_ADR[5]);
  Decoder #(.select(3)) decoder_5 (
    .out0(FP0), .out1(FP1), .out2(FP2), .out3(FP3), .sel(T_ADR[2:0]), .en(and_132_out));  // open: out4, out5, out6, out7
  assign T_BUS = and_133_out ? switch_16_p1 : 8'bz;  // Controlled_Buffer controlled_buffer_16
  and and_133 (and_133_out, FP1, T_RD);
  assign T_BUS = and_134_out ? switch_8_p1 : 8'bz;  // Controlled_Buffer controlled_buffer_17
  and and_134 (and_134_out, FP0, T_RD);
  assign T_BUS = and_135_out ? {pull_resistor_17_node, d_ff_6_q} : 8'bz;  // Controlled_Buffer controlled_buffer_18
  Pull_Resistor pull_resistor_17 (.node(pull_resistor_17_node));
  and and_135 (and_135_out, FP3, T_RD);
  or or_16 (INT0, d_ff_6_q[0], d_ff_6_q[1], d_ff_6_q[2]);
  or or_17 (or_17_out, R, and_136_out);
  and and_136 (and_136_out, FP3, T_WR);
  // also tied to VCC on the sheet: n74193_1_pin4

  // Other names for the same wires on the sheet: ADRL[7:0] = ADDRESS[7:0]; ADRH[7:0] = ADDRESS[15:8]; F0 = alu[0];
  //   F1 = alu[1]; F2 = alu[2]; F3 = alu[3]; F4 = alu[4]; F5 = alu[5]; F6 = alu[6]; F7 = alu[7]; clk_i = clk_e;
  //   LDI = CCLK

  // Notes on the sheet:
  //   State Machine
  //   Instruction Decoder
  //   Address Pointer
  //   Control Unit
  //   IMM
  //   Load/Store Unit
  //   Conditional Logic
  //   4 WR
  //   4 RD
  //   Program Counter
  //   5 WR
  //   6 WR
  //   74181
  //   74181
  //   Transport Buffer
  //   5 RD
  //   6 RD
  //   /Reset
  //   ALU Unit
  //   7 RD
  //   7 WR
  //   Register Unit
  //   Comparator
  //   Register Files
  //   8-15
  //   16-23
  //   Cn Control
  //   Backplane Logic
  //   R/W Logic
  //   Address Byte Joining
  //   Main T_ADR Decoding
  //   Split as needed on unit cards
  //   74182
  //   Front Panel
  //   74193 16-bit PC
  //   Bit Set Comparator
  //   External Connections
endmodule
